# Fritzing sketch Boat_schematic_rigtigt (saved by Fritzing 1.0.3b)
breadboards: 1

parts:
  Servo_gripper_1 = Basic Servo
  Servo_gripper_2 = Basic Servo
  part = DC Power [voltage=5V internal_resistance=0.1Ω]
  IR_receiver = Infrared Proximity Sensor [distance_to_obstacle=50%]
  Thrusters_right = DJI 920 KV Motor
  Thrusters_left = DJI 920 KV Motor
  V12 = DC Power [voltage=12V internal_resistance=0.1Ω]
  ESC_2 = Littlebee 30A ESC
  ESC_1 = Littlebee 30A ESC
  Part1 = Arduino Mega 2560 (Rev3)
  microSD1 = MicroSD Card Module
  U1 = ACS712 [package=so08]
  Mod1 = Amica NodeMCU DEVKIT 1.0

nets:
  GND: Servo_gripper_1.gnd, Servo_gripper_2.gnd, part.V-, IR_receiver.GND, V12.V-, ESC_2.Pin_1, ESC_2.Pin_6, ESC_1.Pin_1, ESC_1.Pin_6, Part1.GND, microSD1.GND, U1.GND, Mod1.pin2, Mod1.pin_29
  5V: Servo_gripper_1.vcc, Servo_gripper_2.vcc, part.V+, IR_receiver.Vcc, Part1.VIN, microSD1.VCC, U1.VCC, Mod1.pin_30
  Ser_in_1: Servo_gripper_1.pulse, Part1.D3_PWM
  Ser_in_2: Servo_gripper_2.pulse, Part1.D4_PWM
  IR: IR_receiver.Vout, Part1.D2_PWM
  N1: Thrusters_right.w, ESC_2.Pin_3
  N2: Thrusters_right.v, ESC_2.Pin_4
  N3: Thrusters_right.u, ESC_2.Pin_5
  N4: Thrusters_left.w, ESC_1.Pin_3
  N5: Thrusters_left.v, ESC_1.Pin_4
  N6: Thrusters_left.u, ESC_1.Pin_5
  12V: V12.V+, U1.IP+
  current_input: ESC_2.Pin_2, ESC_1.Pin_2, U1.IP-
  T2: ESC_2.Pin_8, Part1.D10_PWM
  T1: ESC_1.Pin_8, Part1.D9_PWM
  C_OUT: Part1.A0, U1.VOUT
  esp_write: Part1.D17_PWM/RX2, Mod1.pin4
  ESP_read: Part1.D16_PWM/TX2, Mod1.pin3
  MISO: Part1.D50, microSD1.MISO
  MOSI: Part1.D51, microSD1.MOSI
  SCK: Part1.D52, microSD1.SCK
  CS: Part1.D53, microSD1.CS

custom parts:
  DJI 920 KV Motor: DJI Brushless Outrunner 2212/920K Motor F330-550
  Littlebee 30A ESC: LittleBee 30A 2-4 LiPo Battery ESC Brushless Speed Controller for RC FPV Multicopter.
